// Digital circuit Processor.dig as structural Verilog
module Processor (
  input  clk,
  input  ReStart
);

  wire alu_1_carry, alu_1_neg, alu_1_zero, branch_1_jmp, control_1_absjmp, control_1_alutobus, control_1_brk,
       control_1_imm, control_1_ld, control_1_muxa, control_1_st, control_1_stpc, register_1_p5,
       register_1_p6, register_1_p7;
  wire [2:0] control_1_branch, control_1_muxb;
  wire [3:0] rom_1_d, rom_1_d_2;
  wire [4:0] control_1_aluop;
  wire [6:0] rom_1_d_4;
  wire [8:8] rom_1_d_3;
  wire [15:0] alu_1_y, driver_1_out, imreg_1_imm, multiplexer_1_out, multiplexer_2_out, pc_1_next, pc_1_pc,
       register_1_p8, register_1_p9, signext_1__5d, signext_1__5s, signext_1__9sd;

  PC pc_1 (
    .ALU(alu_1_y), .Clock(clk), .abs(control_1_absjmp), .BRK(control_1_brk), .rel(branch_1_jmp),
    .Next(pc_1_next), .PC(pc_1_pc));
  ROM #(.Bits(16), .Addr_Bits(16)) rom_1 (.A(pc_1_pc), .sel(1'b1), .D({rom_1_d_4, rom_1_d_3[8], rom_1_d_2, rom_1_d}));
  assign driver_1_out = control_1_stpc ? pc_1_next : 16'bz;  // Driver driver_1
  // Register register_1: pin names not known; wires that end beside it: driver_1_out, clk, rom_1_d, rom_1_d_2, register_1_p5, register_1_p6, register_1_p7, register_1_p8, register_1_p9
  ImReg imreg_1 (.inst({rom_1_d_4, rom_1_d_3[8], rom_1_d_2, rom_1_d}), .en(control_1_imm), .C(clk), .imm(imreg_1_imm));
  Control control_1 (
    .Op(rom_1_d_4), .BRKen(ReStart), .stPC(control_1_stpc), .WE(register_1_p5), .imm(control_1_imm),
    .absJmp(control_1_absjmp), .BRK(control_1_brk), .muxB(control_1_muxb), .muxA(control_1_muxa),
    .ALUToBus(control_1_alutobus), .ALUop(control_1_aluop), .Branch(control_1_branch), .st(control_1_st),
    .ld(control_1_ld));  // open: ioW, ioR
  // Probe R0 on register_1_p6
  SignExt signext_1 (
    .inst({rom_1_d_4, rom_1_d_3[8], rom_1_d_2, rom_1_d}), ._5S(signext_1__5s), ._9SD(signext_1__9sd),
    ._5D(signext_1__5d));
  // Probe R1 on register_1_p7
  Multiplexer #(.Selector_Bits(3), .Bits(16)) multiplexer_1 (
    .sel(control_1_muxb), .in_0(register_1_p9), .in_1(imreg_1_imm), .in_2({16{1'b0}}), .in_3(16'hff),
    .in_4(16'hfff), .in_5(signext_1__5s), .in_6(signext_1__9sd), .in_7(signext_1__5d), .out(multiplexer_1_out));
  Multiplexer #(.Bits(16)) multiplexer_2 (
    .sel(control_1_muxa), .in_0(register_1_p8), .in_1(register_1_p9), .out(multiplexer_2_out));
  ALU alu_1 (
    .A(multiplexer_2_out), .B(multiplexer_1_out), .Op(control_1_aluop), .Ci(clk), .Y(alu_1_y),
    .Zero(alu_1_zero), .Neg(alu_1_neg), .Carry(alu_1_carry));
  assign driver_1_out = control_1_alutobus ? alu_1_y : 16'bz;  // Driver driver_2
  Branch branch_1 (.Z(alu_1_zero), .N(alu_1_neg), .C(alu_1_carry), .ctrl(control_1_branch), .jmp(branch_1_jmp));
  RAMDualPort #(.Bits(16), .Addr_Bits(16)) ramdualport_1 (
    .A(alu_1_y), .Din(register_1_p9), .str(control_1_st), .C(clk), .ld(control_1_ld), .D(driver_1_out));

  // Notes on the sheet:
  //   contents of rom_1 (hex, n*v repeats v):
  //   65536
  //   5123
  //   5137
  //   1025
  //   31744
  //   16
endmodule
